# Fritzing sketch photoreacteur (saved by Fritzing 0.9.3b)
breadboards: 1

parts:
  Composant1 = Arduino Nano (Rev3.0)
  U1 = ENCODER_2LED [package=encoder_led_2]
  Composant2 = FemtoBuck LED Driver
  Grove1 = Grove OLED 128x96
  U3 = Voltage Regulator LDO [package=sot23-5]
  F1 = Fan - Ventilador [package=THT]
  JP2 = Header 2 [package=molex-1x2_lock]
  U4 = Molex Picoblade Series Header [part_number=0532610219 package=Picoblade-53261-0219]
  J2 = Power Jack [package=power_jack_smd]
  LED1 = Super Flux LED blue [color=Blue]
  R1 = PHOTOCELL [package=photocell-kit]
  S1 = H-Bridge with L298N
  S2 = SPST Switch [package=r_sw_th]
  R2 = Resistor [tolerance=±5% resistance=220 package=THT]
  U5 = TMP36 [package=to-92]

nets:
  GND: Composant1.GND, U1.+R, U1.B, Composant2.D-, Grove1.GND, U3.GND, S1.GND, S1.IN2, S2.P, R2.Pin_1, U5.GND
  N1: Composant1.D2, U1.A
  N2: Composant1.D3, U1.+G
  N3: Composant1.D4, U1.SW
  N4: Composant1.D5, U1.C
  N5: Composant1.D6, U1.-
  N6: Composant1.D9, Composant2.D+
  N7: Composant1.D11/MOSI, S1.ENA
  5V: Composant1.5V, Grove1.VCC, U3.EN, R1.P$1, S1.5V, S1.IN1, U5.VCC
  N8: Composant1.A5, Grove1.SCL
  N9: Composant1.A4, Grove1.SDA
  N10: Composant1.A3, R1.P$2, R2.Pin_0
  N11: Composant1.A2, U5.VOUT
  N12: Composant2.PGND, U3.OUT
  N13: Composant2.VIN, U3.BP
  N14: Composant2.OUT+, JP2.1
  N15: Composant2.OUT-, JP2.2
  N16: F1.5V, S1.M2-02
  N17: F1.GND, S1.M2-01
  N18: U4.1, LED1.cathode
  N19: U4.2, LED1.anode
  N20: J2.GND, J2.GNDBREAK, S2.S

custom parts:
  Fan - Ventilador: Ventilador de 2 pines, se encuentra comunmente en computadoras de escritorio
  H-Bridge with L298N: h-bridge
